// Logisim project Fat_Cat_CPU.circ as structural Verilog: 10 circuits, main circuit Fat_Cat_CPU
module Fat_Cat_CPU (
);

  wire alu_1_p6, alu_1_p7, alu_1_p8, alu_1_p9, and_1_out, Carry_Register_q, clk_out, Halt_qn,
       instruction_decoder_1_addr_is_reg, instruction_decoder_1_isimm, instruction_decoder_1_mem_read,
       instruction_decoder_1_mem_write, instruction_decoder_1_pass_carry, instruction_decoder_1_reg_write,
       multiplexer_1_out, overflow_register_q, reset_out, sign_register_q, zero_register_q;
  wire [1:0] instruction_decoder_1_wb_sel;
  wire [2:0] instruction_decoder_1_rd, instruction_decoder_1_rs, instruction_decoder_1_rt;
  wire [3:0] alu_1_p4;
  wire [4:0] instruction_decoder_1_imm5, instruction_memory_data;
  wire [7:0] alu_1_p1, alu_1_p5, bit_extender_1_out, data_memory_dout, instruction_decoder_1_addr8,
       multiplexer_2_out, multiplexer_3_out, multiplexer_4_out, register_file_1_rd2;
  wire [10:0] adder_1_out, pc_next_q, pc_q, undriven;
  wire [15:5] instruction_memory_data_2;

  Clock clk (.out(clk_out));
  Button reset (.out(reset_out));
  D_Flip_Flop Halt (.clk(clk_out), .Qn(Halt_qn));  // open: D, Q, preset, reset
  assign bit_extender_1_out = {{3{1'b0}}, instruction_decoder_1_imm5};  // Bit_Extender bit_extender_1
  Multiplexer multiplexer_1 (
    .in0(1'b0), .in1(Carry_Register_q), .out(multiplexer_1_out), .sel(instruction_decoder_1_pass_carry));
  Multiplexer #(.width(8)) multiplexer_2 (
    .in0(register_file_1_rd2), .in1(bit_extender_1_out), .out(multiplexer_2_out),
    .sel(instruction_decoder_1_isimm));
  and and_1 (and_1_out, clk_out, Halt_qn);
  // ALU alu_1: pin names not known; wires that end beside it: alu_1_p1, multiplexer_2_out, multiplexer_1_out, alu_1_p4, alu_1_p5, alu_1_p6, alu_1_p7, alu_1_p8, alu_1_p9
  D_Flip_Flop zero_register (
    .D(alu_1_p6), .clk(and_1_out), .Q(zero_register_q), .reset(reset_out));  // open: Qn, preset
  D_Flip_Flop Carry_Register (
    .D(alu_1_p7), .clk(and_1_out), .Q(Carry_Register_q), .reset(reset_out));  // open: Qn, preset
  D_Flip_Flop sign_register (
    .D(alu_1_p8), .clk(and_1_out), .Q(sign_register_q), .reset(reset_out));  // open: Qn, preset
  Register #(.width(11)) pc (.D(pc_next_q), .clk(clk_out), .Q(pc_q), .clr(reset_out));  // open: en
  Register #(.width(11)) pc_next (.D(undriven), .clk(clk_out), .Q(pc_next_q), .clr(reset_out));  // open: en
  T_Flip_Flop overflow_register (
    .T(alu_1_p9), .clk(and_1_out), .Q(overflow_register_q), .reset(reset_out));  // open: Qn, preset
  ROM #(.addrWidth(11), .dataWidth(16)) instruction_memory (
    .addr(pc_q), .data({instruction_memory_data_2, instruction_memory_data}));
  Adder #(.width(11)) adder_1 (.a(pc_q), .b({11{1'b0}}), .out(adder_1_out), .cin(1'b1));  // open: cout
  Multiplexer #(.width(8)) multiplexer_3 (
    .in0(instruction_decoder_1_addr8), .in1(alu_1_p1), .out(multiplexer_3_out),
    .sel(instruction_decoder_1_addr_is_reg));
  Multiplexer #(.select(2), .width(8)) multiplexer_4 (
    .in0(alu_1_p5), .in1(instruction_decoder_1_addr8), .in2(data_memory_dout), .in3(adder_1_out[7:0]),
    .out(multiplexer_4_out), .sel(instruction_decoder_1_wb_sel));
  branch_logic branch_logic_1 (
    .zero(zero_register_q), .sign(sign_register_q), .overflow(overflow_register_q),
    .opcode(instruction_memory_data));  // open: branch_taken
  RAM #(.clearpin("true")) data_memory (
    .addr(multiplexer_3_out), .we(instruction_decoder_1_mem_write), .oe(instruction_decoder_1_mem_read),
    .clk(clk_out), .dout(data_memory_dout), .clr(reset_out));  // open: din
  instruction_decoder instruction_decoder_1 (
    .instruction({instruction_memory_data_2, instruction_memory_data}), .addr8(instruction_decoder_1_addr8),
    .wb_sel(instruction_decoder_1_wb_sel), .alu_opcode(alu_1_p4),
    .reg_write(instruction_decoder_1_reg_write), .isImm(instruction_decoder_1_isimm),
    .pass_carry(instruction_decoder_1_pass_carry), .rt(instruction_decoder_1_rt),
    .addr_is_reg(instruction_decoder_1_addr_is_reg), .mem_read(instruction_decoder_1_mem_read),
    .mem_write(instruction_decoder_1_mem_write), .imm5(instruction_decoder_1_imm5),
    .rs(instruction_decoder_1_rs), .rd(instruction_decoder_1_rd));  // open: halt, addr11, jump, branch
  register_file register_file_1 (
    .we(instruction_decoder_1_reg_write), .wd(multiplexer_4_out), .wa(instruction_decoder_1_rd),
    .clock(and_1_out), .reset(reset_out), .ra2(instruction_decoder_1_rt), .ra1(instruction_decoder_1_rs),
    .rd1(alu_1_p1), .rd2(register_file_1_rd2));

  // Notes on the sheet:
  //   contents of instruction_memory (hex, n*v repeats v):
  //   1ad1 1812 c143
endmodule

module instruction_decoder (
  input  [15:0] instruction,
  output [2:0] rt,
  output [2:0] rs,
  output [4:0] imm5,
  output [7:0] addr8,
  output [10:0] addr11,
  output [2:0] rd,
  output [3:0] alu_opcode,
  output halt,
  output isImm,
  output branch,
  output jump,
  output mem_write,
  output reg_write,
  output addr_is_reg,
  output mem_read,
  output pass_carry,
  output [1:0] wb_sel
);

  wire and_1_out, decoder_1_out1, decoder_1_out2, decoder_1_out3, decoder_1_out4, decoder_1_out5,
       decoder_1_out6, decoder_1_out7, decoder_1_out8, decoder_1_out9, decoder_1_out10, decoder_1_out11,
       decoder_1_out12, decoder_1_out13, decoder_1_out14, decoder_1_out15, decoder_1_out17, decoder_1_out18,
       decoder_1_out19, decoder_1_out20, decoder_1_out21, decoder_1_out22, decoder_1_out23, decoder_1_out24,
       decoder_1_out25, decoder_1_out26, decoder_1_out27, decoder_1_out28, decoder_1_out29;
  wire [4:0] xnor_1_out, xnor_2_out;

  Multiplexer #(.select(5)) multiplexer_1 (.sel(instruction[4:0]));  // open: in0, in1, in2, in3, in4, in5, in6, in7, in8, in9, in10, in11, in12, in13, in14, in15, in16, in17, in18, in19, in20, in21, in22, in23, in24, in25, in26, in27, in28, in29, in30, in31, out
  Multiplexer #(.width(4)) multiplexer_2 (
    .in0(instruction[4:1]), .in1(4'b0000), .out(alu_opcode), .sel(instruction[0]));
  Decoder #(.enable("false"), .select(5)) decoder_1 (
    .out0(halt), .out1(decoder_1_out1), .out2(decoder_1_out2), .out3(decoder_1_out3), .out4(decoder_1_out4),
    .out5(decoder_1_out5), .out6(decoder_1_out6), .out7(decoder_1_out7), .out8(decoder_1_out8),
    .out9(decoder_1_out9), .out10(decoder_1_out10), .out11(decoder_1_out11), .out12(decoder_1_out12),
    .out13(decoder_1_out13), .out14(decoder_1_out14), .out15(decoder_1_out15), .out17(decoder_1_out17),
    .out18(decoder_1_out18), .out19(decoder_1_out19), .out20(decoder_1_out20), .out21(decoder_1_out21),
    .out22(decoder_1_out22), .out23(decoder_1_out23), .out24(decoder_1_out24), .out25(decoder_1_out25),
    .out26(decoder_1_out26), .out27(decoder_1_out27), .out28(decoder_1_out28), .out29(decoder_1_out29),
    .out30(pass_carry), .sel(instruction[4:0]));  // open: out16, out31
  Multiplexer #(.select(5), .width(2)) multiplexer_3 (
    .in0(2'b00), .in1(2'b01), .in2(2'b00), .in3(2'b10), .in4(2'b00), .in5(2'b00), .in6(2'b00), .in7(2'b00),
    .in8(2'b00), .in9(2'b00), .in10(2'b00), .in11(2'b11), .in12(2'b00), .in13(2'b00), .in14(2'b01),
    .in15(2'b00), .in16(2'b00), .in17(2'b00), .in18(2'b00), .in19(2'b00), .in20(2'b00), .in21(2'b00),
    .in22(2'b00), .in23(2'b00), .in24(2'b00), .in25(2'b00), .in26(2'b00), .in27(2'b00), .in28(2'b00),
    .in29(2'b00), .in30(2'b00), .in31(2'b00), .out(wb_sel));  // open: sel
  assign xnor_1_out = ~(instruction[4:0] ^ 5'b00010);  // XNOR_Gate xnor_1, 5 bits wide
  assign xnor_2_out = ~(instruction[4:0] ^ 5'b01111);  // XNOR_Gate xnor_2, 5 bits wide
  and and_1 (and_1_out, xnor_1_out[0], xnor_1_out[1], xnor_1_out[2], xnor_1_out[3], xnor_1_out[4]);
  and and_2 (and_1_out, xnor_2_out[0], xnor_2_out[1], xnor_2_out[2], xnor_2_out[3], xnor_2_out[4]);
  or or_1 (reg_write, decoder_1_out1, decoder_1_out3, decoder_1_out11, decoder_1_out13, decoder_1_out14, decoder_1_out17, decoder_1_out18, decoder_1_out19, decoder_1_out20, decoder_1_out21, decoder_1_out22, decoder_1_out23, decoder_1_out24, decoder_1_out25, decoder_1_out26, decoder_1_out27, decoder_1_out28, decoder_1_out29, pass_carry);
  or or_2 (isImm, decoder_1_out3, decoder_1_out28, decoder_1_out29);
  Multiplexer #(.width(3)) multiplexer_4 (.in0(instruction[10:8]), .in1(instruction[15:13]), .out(rt), .sel(and_1_out));
  or or_3 (branch, decoder_1_out4, decoder_1_out5, decoder_1_out6, decoder_1_out7, decoder_1_out8, decoder_1_out9);
  ExactlyOne xor_1 (.out(jump), .in0(decoder_1_out10), .in1(decoder_1_out11), .in2(decoder_1_out12));
  or or_4 (addr_is_reg, decoder_1_out14, decoder_1_out15);
  or or_5 (mem_read, decoder_1_out1, decoder_1_out14);
  or or_6 (mem_write, decoder_1_out2, decoder_1_out15);

  assign addr8 = instruction[12:5];
  assign addr11 = instruction[15:5];
  assign imm5 = instruction[12:8];
  assign rd = instruction[15:13];
  assign rs = instruction[7:5];
endmodule

module register_file (
  input  clock,
  input  reset,
  input  [7:0] wd,
  input  [2:0] ra1,
  input  we,
  input  [2:0] wa,
  input  [2:0] ra2,
  output [7:0] rd1,
  output [7:0] rd2
);

  wire decoder_1_out1, decoder_1_out2, decoder_1_out3, decoder_1_out4, decoder_1_out5, decoder_1_out6,
       decoder_1_out7;
  wire [7:0] register_1_q, register_2_q, register_3_q, register_4_q, register_5_q, register_6_q,
       register_7_q, register_8_q;

  Pull_Resistor pull_resistor_1 (.node(reset));
  Decoder #(.select(3)) decoder_1 (
    .out1(decoder_1_out1), .out2(decoder_1_out2), .out3(decoder_1_out3), .out4(decoder_1_out4),
    .out5(decoder_1_out5), .out6(decoder_1_out6), .out7(decoder_1_out7), .sel(wa), .en(we));  // open: out0
  Register register_1 (.D(wd), .en(1'b0), .clk(clock), .Q(register_1_q), .clr(reset));
  Register register_2 (.D(wd), .en(decoder_1_out2), .clk(clock), .Q(register_2_q), .clr(reset));
  Register register_3 (.D(wd), .en(decoder_1_out4), .clk(clock), .Q(register_3_q), .clr(reset));
  Register register_4 (.D(wd), .en(decoder_1_out6), .clk(clock), .Q(register_4_q), .clr(reset));
  Register register_5 (.D(wd), .en(decoder_1_out1), .clk(clock), .Q(register_5_q), .clr(reset));
  Register register_6 (.D(wd), .en(decoder_1_out3), .clk(clock), .Q(register_6_q), .clr(reset));
  Register register_7 (.D(wd), .en(decoder_1_out5), .clk(clock), .Q(register_7_q), .clr(reset));
  Register register_8 (.D(wd), .en(decoder_1_out7), .clk(clock), .Q(register_8_q), .clr(reset));
  Multiplexer #(.select(3), .width(8)) multiplexer_1 (
    .in0(register_1_q), .in1(register_5_q), .in2(register_2_q), .in3(register_6_q), .in4(register_3_q),
    .in5(register_7_q), .in6(register_4_q), .in7(register_8_q), .out(rd1), .sel(ra1));
  Multiplexer #(.select(3), .width(8)) multiplexer_2 (
    .in0(register_1_q), .in1(register_5_q), .in2(register_2_q), .in3(register_6_q), .in4(register_3_q),
    .in5(register_7_q), .in6(register_4_q), .in7(register_8_q), .out(rd2), .sel(ra2));
endmodule

module ALU (
  input  [7:0] a,
  input  [7:0] b,
  input  [3:0] opcode,
  input  carry_in,
  output [7:0] result,
  output carry,
  output zero,
  output sign,
  output overflow
);

  wire ADC_c_out, ADC_overflow, ADD_c_out, ADD_overflow, CMP_c_out, CMP_overflow, MUL_carry,
       pull_resistor_1_node, pull_resistor_2_node, pull_resistor_3_node, pull_resistor_4_node, Sub_c_out,
       Sub_overflow, xor_2_out, xor_3_out;
  wire [2:0] bit_extender_1_out;
  wire [6:0] CMP_sum;
  wire [7:0] ADC_sum, ADD_sum, and_1_out, MUL_product, NEG_sum, not_1_out, not_2_out, not_3_out, not_4_out,
       or_1_out, shifter_1_out, shifter_2_out, shifter_3_out, Sub_sum, xor_1_out;

  assign not_1_out = ~b;  // NOT_Gate not_1, 8 bits wide
  assign and_1_out = a & b;  // AND_Gate and_1, 8 bits wide
  assign or_1_out = a | b;  // OR_Gate or_1, 8 bits wide
  assign not_2_out = ~a;  // NOT_Gate not_2, 8 bits wide
  assign xor_1_out = a ^ b;  // XOR_Gate xor_1, 8 bits wide
  Bit_Extender #(.out_width(3)) bit_extender_1 (.in(b), .out(bit_extender_1_out));
  Pull_Resistor pull_resistor_1 (.node(pull_resistor_1_node));
  Pull_Resistor #(.pull(1)) pull_resistor_2 (.node(pull_resistor_2_node));
  assign not_3_out = ~a;  // NOT_Gate not_3, 8 bits wide
  Pull_Resistor #(.pull(1)) pull_resistor_3 (.node(pull_resistor_3_node));
  assign not_4_out = ~b;  // NOT_Gate not_4, 8 bits wide
  Pull_Resistor #(.pull(1)) pull_resistor_4 (.node(pull_resistor_4_node));
  Shifter shifter_1 (.in(a), .\dist (bit_extender_1_out), .out(shifter_1_out));
  Shifter #(.shift("lr")) shifter_2 (.in(a), .\dist (bit_extender_1_out), .out(shifter_2_out));
  Shifter #(.shift("ar")) shifter_3 (.in(a), .\dist (bit_extender_1_out), .out(shifter_3_out));
  Multiplexer #(.select(4), .width(8)) multiplexer_1 (
    .in0(a), .in1(and_1_out), .in2(or_1_out), .in3(not_2_out), .in4(xor_1_out), .in5(shifter_1_out),
    .in6(shifter_2_out), .in7(shifter_3_out), .in8(ADD_sum), .in9(Sub_sum), .in10(MUL_product),
    .in11(NEG_sum), .in12(ADD_sum), .in13(MUL_product), .in14(ADC_sum), .in15({8{1'b0}}), .out(result),
    .sel(opcode));
  Ripple_Carry_Adder_8_bit ADD (
    .a(a), .b(b), .c_in(pull_resistor_1_node), .c_out(ADD_c_out), .sum(ADD_sum), .overflow(ADD_overflow));
  Ripple_Carry_Adder_8_bit Sub (
    .a(a), .b(not_1_out), .c_in(pull_resistor_2_node), .c_out(Sub_c_out), .sum(Sub_sum),
    .overflow(Sub_overflow));
  Shift_Add_Multiplier MUL (.a(a), .b(b), .product(MUL_product), .carry(MUL_carry));
  Ripple_Carry_Adder_8_bit NEG (
    .a(not_3_out), .b({8{1'b0}}), .c_in(pull_resistor_3_node), .sum(NEG_sum));  // open: c_out, overflow
  Ripple_Carry_Adder_8_bit ADC (
    .a(a), .b(b), .c_in(carry_in), .c_out(ADC_c_out), .sum(ADC_sum), .overflow(ADC_overflow));
  Ripple_Carry_Adder_8_bit CMP (
    .a(a), .b(not_4_out), .c_in(pull_resistor_4_node), .c_out(CMP_c_out), .sum({sign, CMP_sum}),
    .overflow(CMP_overflow));
  nor nor_1 (zero, CMP_sum[0], CMP_sum[1], CMP_sum[2], CMP_sum[3], CMP_sum[4], CMP_sum[5], CMP_sum[6], sign);
  xor xor_2 (xor_2_out, sign, a[7]);
  xor xor_3 (xor_3_out, a[7], b[7]);
  Multiplexer #(.select(4)) multiplexer_2 (
    .in0(1'b0), .in1(1'b0), .in2(1'b0), .in3(1'b0), .in4(1'b0), .in5(1'b0), .in6(1'b0), .in7(1'b0),
    .in8(ADD_c_out), .in9(Sub_c_out), .in10(MUL_carry), .in11(1'b0), .in12(ADD_c_out), .in13(MUL_carry),
    .in14(ADC_c_out), .in15(CMP_c_out), .out(carry), .sel(opcode));
  and and_2 (overflow, xor_2_out, xor_3_out);

  // Notes on the sheet:
  //   ADD
endmodule

module branch_logic (
  input  zero,
  input  sign,
  input  overflow,
  input  [4:0] opcode,
  output branch_taken
);

  wire and_1_out, not_1_out, not_2_out, or_1_out, xor_1_out;

  xor xor_1 (xor_1_out, sign, overflow);
  not not_1 (not_1_out, xor_1_out);
  not not_2 (not_2_out, zero);
  and and_1 (and_1_out, not_2_out, not_1_out);
  or or_1 (or_1_out, zero, xor_1_out);
  Multiplexer #(.select(5)) multiplexer_1 (
    .in4(zero), .in5(not_2_out), .in6(xor_1_out), .in7(and_1_out), .in8(or_1_out), .in9(not_1_out),
    .out(branch_taken), .sel(opcode));  // open: in0, in1, in2, in3, in10, in11, in12, in13, in14, in15, in16, in17, in18, in19, in20, in21, in22, in23, in24, in25, in26, in27, in28, in29, in30, in31
endmodule

module Ripple_Carry_Adder_8_bit (
  input  [7:0] a,
  input  [7:0] b,
  input  c_in,
  output c_out,
  output [7:0] sum,
  output overflow
);

  wire full_adder_1_c_out, full_adder_2_c_out, full_adder_3_c_out, full_adder_4_c_out, full_adder_5_c_out,
       full_adder_6_c_out, full_adder_7_c_out, xnor_1_out, xor_1_out;

  Pull_Resistor pull_resistor_1 (.node(c_in));
  Full_Adder full_adder_1 (.a(a[0]), .b(b[0]), .c_in(c_in), .sum(sum[0]), .c_out(full_adder_1_c_out));
  Full_Adder full_adder_2 (.a(a[1]), .b(b[1]), .c_in(full_adder_1_c_out), .sum(sum[1]), .c_out(full_adder_2_c_out));
  Full_Adder full_adder_3 (.a(a[2]), .b(b[2]), .c_in(full_adder_2_c_out), .sum(sum[2]), .c_out(full_adder_3_c_out));
  Full_Adder full_adder_4 (.a(a[3]), .b(b[3]), .c_in(full_adder_3_c_out), .sum(sum[3]), .c_out(full_adder_4_c_out));
  Full_Adder full_adder_5 (.a(a[4]), .b(b[4]), .c_in(full_adder_4_c_out), .sum(sum[4]), .c_out(full_adder_5_c_out));
  Full_Adder full_adder_6 (.a(a[5]), .b(b[5]), .c_in(full_adder_5_c_out), .sum(sum[5]), .c_out(full_adder_6_c_out));
  Full_Adder full_adder_7 (.a(a[6]), .b(b[6]), .c_in(full_adder_6_c_out), .sum(sum[6]), .c_out(full_adder_7_c_out));
  Full_Adder full_adder_8 (.a(a[7]), .b(b[7]), .c_in(full_adder_7_c_out), .sum(sum[7]), .c_out(c_out));
  xor xor_1 (xor_1_out, sum[7], a[7]);
  xnor xnor_1 (xnor_1_out, a[7], b[7]);
  and and_1 (overflow, xor_1_out, xnor_1_out);
endmodule

module Full_Adder (
  input  a,
  input  b,
  input  c_in,
  output sum,
  output c_out
);

  wire and_1_out, and_2_out, and_3_out;

  and and_1 (and_1_out, a, c_in);
  and and_2 (and_2_out, a, b);
  and and_3 (and_3_out, b, c_in);
  xor xor_1 (sum, a, b, c_in);
  or or_1 (c_out, and_1_out, and_2_out, and_3_out);
endmodule

module Shift_Add_Multiplier (
  input  [7:0] a,
  input  [7:0] b,
  output [7:0] product,
  output carry
);

  wire or_1_out, or_2_out, or_3_out, or_4_out, or_5_out, or_6_out, ripple_carry_adder_8_bit_1_c_out,
       ripple_carry_adder_8_bit_2_c_out, ripple_carry_adder_8_bit_3_c_out, ripple_carry_adder_8_bit_4_c_out,
       ripple_carry_adder_8_bit_5_c_out, ripple_carry_adder_8_bit_6_c_out, ripple_carry_adder_8_bit_7_c_out;
  wire [7:0] and_1_out, and_2_out, and_3_out, and_4_out, and_5_out, and_6_out, and_7_out, and_8_out,
       bit_extender_1_out, bit_extender_2_out, bit_extender_3_out, bit_extender_4_out, bit_extender_5_out,
       bit_extender_6_out, bit_extender_7_out, bit_extender_8_out, ripple_carry_adder_8_bit_1_sum,
       ripple_carry_adder_8_bit_2_sum, ripple_carry_adder_8_bit_3_sum, ripple_carry_adder_8_bit_4_sum,
       ripple_carry_adder_8_bit_5_sum, ripple_carry_adder_8_bit_6_sum, shifter_1_out, shifter_2_out,
       shifter_3_out, shifter_4_out, shifter_5_out, shifter_6_out, shifter_7_out;

  assign bit_extender_1_out = {{7{a[0]}}, a[0]};  // Bit_Extender bit_extender_1
  assign and_1_out = bit_extender_1_out & b;  // AND_Gate and_1, 8 bits wide
  assign bit_extender_2_out = {{7{a[1]}}, a[1]};  // Bit_Extender bit_extender_2
  assign and_2_out = bit_extender_2_out & b;  // AND_Gate and_2, 8 bits wide
  assign bit_extender_3_out = {{7{a[2]}}, a[2]};  // Bit_Extender bit_extender_3
  Shifter shifter_1 (.in(and_2_out), .\dist (3'b001), .out(shifter_1_out));
  assign and_3_out = bit_extender_3_out & b;  // AND_Gate and_3, 8 bits wide
  Ripple_Carry_Adder_8_bit ripple_carry_adder_8_bit_1 (
    .a(shifter_1_out), .b(and_1_out), .c_out(ripple_carry_adder_8_bit_1_c_out),
    .sum(ripple_carry_adder_8_bit_1_sum));  // open: c_in, overflow
  assign bit_extender_4_out = {{7{a[3]}}, a[3]};  // Bit_Extender bit_extender_4
  assign and_4_out = bit_extender_4_out & b;  // AND_Gate and_4, 8 bits wide
  Shifter shifter_2 (.in(and_3_out), .\dist (3'b010), .out(shifter_2_out));
  or or_1 (or_1_out, and_3_out[6], and_3_out[7]);
  assign bit_extender_5_out = {{7{a[4]}}, a[4]};  // Bit_Extender bit_extender_5
  Shifter shifter_3 (.in(and_4_out), .\dist (3'b011), .out(shifter_3_out));
  assign and_5_out = bit_extender_5_out & b;  // AND_Gate and_5, 8 bits wide
  Ripple_Carry_Adder_8_bit ripple_carry_adder_8_bit_2 (
    .a(shifter_2_out), .b(ripple_carry_adder_8_bit_1_sum), .c_in(ripple_carry_adder_8_bit_1_c_out),
    .c_out(ripple_carry_adder_8_bit_2_c_out), .sum(ripple_carry_adder_8_bit_2_sum));  // open: overflow
  or or_2 (or_2_out, and_4_out[5], and_4_out[6], and_4_out[7]);
  assign bit_extender_6_out = {{7{a[5]}}, a[5]};  // Bit_Extender bit_extender_6
  Shifter shifter_4 (.in(and_5_out), .\dist (3'b100), .out(shifter_4_out));
  or or_3 (or_3_out, and_5_out[4], and_5_out[5], and_5_out[6], and_5_out[7]);
  assign bit_extender_7_out = {{7{a[6]}}, a[6]};  // Bit_Extender bit_extender_7
  assign and_6_out = bit_extender_6_out & b;  // AND_Gate and_6, 8 bits wide
  Shifter shifter_5 (.in(and_6_out), .\dist (3'b101), .out(shifter_5_out));
  assign and_7_out = bit_extender_7_out & b;  // AND_Gate and_7, 8 bits wide
  Ripple_Carry_Adder_8_bit ripple_carry_adder_8_bit_3 (
    .a(shifter_3_out), .b(ripple_carry_adder_8_bit_2_sum), .c_in(ripple_carry_adder_8_bit_2_c_out),
    .c_out(ripple_carry_adder_8_bit_3_c_out), .sum(ripple_carry_adder_8_bit_3_sum));  // open: overflow
  assign bit_extender_8_out = {{7{a[7]}}, a[7]};  // Bit_Extender bit_extender_8
  Shifter shifter_6 (.in(and_7_out), .\dist (3'b110), .out(shifter_6_out));
  assign and_8_out = bit_extender_8_out & b;  // AND_Gate and_8, 8 bits wide
  Shifter shifter_7 (.in(and_8_out), .\dist (3'b111), .out(shifter_7_out));
  or or_4 (or_4_out, and_6_out[3], and_6_out[4], and_6_out[5], and_6_out[6], and_6_out[7]);
  Ripple_Carry_Adder_8_bit ripple_carry_adder_8_bit_4 (
    .a(shifter_4_out), .b(ripple_carry_adder_8_bit_3_sum), .c_in(ripple_carry_adder_8_bit_3_c_out),
    .c_out(ripple_carry_adder_8_bit_4_c_out), .sum(ripple_carry_adder_8_bit_4_sum));  // open: overflow
  or or_5 (or_5_out, and_7_out[2], and_7_out[3], and_7_out[4], and_7_out[5], and_7_out[6], and_7_out[7]);
  Ripple_Carry_Adder_8_bit ripple_carry_adder_8_bit_5 (
    .a(shifter_5_out), .b(ripple_carry_adder_8_bit_4_sum), .c_in(ripple_carry_adder_8_bit_4_c_out),
    .c_out(ripple_carry_adder_8_bit_5_c_out), .sum(ripple_carry_adder_8_bit_5_sum));  // open: overflow
  or or_6 (or_6_out, and_8_out[1], and_8_out[2], and_8_out[3], and_8_out[4], and_8_out[5], and_8_out[6], and_8_out[7]);
  Ripple_Carry_Adder_8_bit ripple_carry_adder_8_bit_6 (
    .a(shifter_6_out), .b(ripple_carry_adder_8_bit_5_sum), .c_in(ripple_carry_adder_8_bit_5_c_out),
    .c_out(ripple_carry_adder_8_bit_6_c_out), .sum(ripple_carry_adder_8_bit_6_sum));  // open: overflow
  Ripple_Carry_Adder_8_bit ripple_carry_adder_8_bit_7 (
    .a(shifter_7_out), .b(ripple_carry_adder_8_bit_6_sum), .c_in(ripple_carry_adder_8_bit_6_c_out),
    .c_out(ripple_carry_adder_8_bit_7_c_out), .sum(product));  // open: overflow
  or or_7 (carry, ripple_carry_adder_8_bit_7_c_out, ripple_carry_adder_8_bit_6_c_out, ripple_carry_adder_8_bit_5_c_out, ripple_carry_adder_8_bit_4_c_out, ripple_carry_adder_8_bit_3_c_out, ripple_carry_adder_8_bit_2_c_out, ripple_carry_adder_8_bit_1_c_out, or_6_out, or_5_out, or_4_out, or_3_out, or_2_out, or_1_out, and_2_out[7]);
endmodule

module ALU_Testbench (
  input  [7:0] a,
  input  [7:0] b,
  input  carry_in,
  input  [3:0] opcode,
  output [7:0] result,
  output out_6,
  output out_7,
  output out_8,
  output out_9
);

  // Probe on a
  // Probe on b
  // Probe on result
  // Probe on result
  ALU alu_1 (
    .carry_in(carry_in), .opcode(opcode), .a(a), .b(b), .zero(out_6), .sign(out_8), .overflow(out_9),
    .carry(out_7), .result(result));
endmodule

module Register_file_testbench (
  input  in_1,
  input  [7:0] in_2,
  input  [2:0] in_3,
  input  [2:0] in_4,
  input  [2:0] in_5,
  output [7:0] out_6,
  output [7:0] out_7
);

  wire button_1_out, clock_1_out;

  Button button_1 (.out(button_1_out));
  Clock clock_1 (.out(clock_1_out));
  register_file register_file_1 (
    .we(in_1), .wd(in_2), .wa(in_3), .clock(clock_1_out), .reset(button_1_out), .ra2(in_5), .ra1(in_4),
    .rd1(out_6), .rd2(out_7));
endmodule
